# Fritzing sketch schema (saved by Fritzing 0.9.3b)
breadboards: 2

parts:
  WeMos_D1_Mini1 = WeMos D1 Mini
  U1 = 74HC4051 [package=so16]
  R1 = Photocell (LDR) [package=THT]
  R2 = Photocell (LDR) [package=THT]
  R3 = Resistor [tolerance=±5% resistance=10k package="2512 [SMD]"]
  R4 = Resistor [tolerance=±5% resistance=10k package="2512 [SMD]"]

nets:
  N1: WeMos_D1_Mini1.3V3, R1.pin_0, R2.pin_0
  N2: WeMos_D1_Mini1.D7, U1.VDD
  N3: WeMos_D1_Mini1.G, R3.Pin_1, R4.Pin_1
  N4: R1.pin_1, R4.Pin_0
  N5: R2.pin_1, R3.Pin_0
